// Logisim project Innovative.circ as structural Verilog: 1 circuit, main circuit main
module main (
  input  in_1,
  input  in_2,
  input  in_3,
  input  in_4,
  input  in_5,
  input  in_6,
  output [6:0] out_7,
  output [11:0] out_8
);

  wire and_1_out, and_2_out, and_3_out, and_4_out, clock_1_out, decoder_1_out0, decoder_1_out1,
       decoder_1_out2, decoder_1_out3, decoder_1_out4, decoder_2_out0, decoder_2_out1, decoder_2_out2,
       decoder_2_out3, decoder_2_out4, decoder_2_out5, not_1_out, not_3_out, not_4_out, not_5_out, or_1_out,
       or_2_out, or_3_out, register_4_q;
  wire [6:0] counter_2_q;
  wire [11:0] counter_1_q, multiplexer_4_out;
  wire [15:0] controlled_buffer_1_out, controlled_buffer_2_out, controlled_buffer_3_out,
       controlled_buffer_4_out, controlled_buffer_5_out, controlled_buffer_6_out, controlled_buffer_7_out,
       multiplexer_1_out, multiplexer_2_out, multiplexer_3_out, multiplier_1_out, nor_1_out, not_2_out,
       ram_1_data, register_1_q, register_2_q, register_3_q, xor_1_out;

  and and_1 (and_1_out, register_4_q, decoder_2_out5);
  Multiplexer #(.select(3), .width(16)) multiplexer_1 (
    .in0({ram_1_data[15], out_7[5:3], ram_1_data[11:0]}), .in1(register_1_q), .in2(register_2_q),
    .in3(register_3_q), .in4({{4{in_3}}, ram_1_data[11:0]}), .out(multiplexer_1_out), .sel(out_8[5:3]));  // open: in5, in6, in7, en
  Multiplexer #(.select(3), .width(16)) multiplexer_2 (
    .in0({ram_1_data[15], out_7[5:3], ram_1_data[11:0]}), .in1(register_1_q), .in2(register_2_q),
    .in3(register_3_q), .in4({{4{in_3}}, ram_1_data[11:0]}), .out(multiplexer_2_out), .sel(out_8[8:6]));  // open: in5, in6, in7, en
  Counter #(.width(12), .max('hfff), .trigger("falling")) counter_1 (
    .load(in_1), .count(1'b1), .Q(counter_1_q), .clk(not_1_out), .clr(in_2));  // open: D, carry
  not not_1 (not_1_out, and_2_out);
  assign controlled_buffer_1_out = decoder_1_out1 ? multiplexer_1_out : 16'bz;  // Controlled_Buffer controlled_buffer_1
  assign controlled_buffer_2_out = decoder_1_out2 ? multiplexer_1_out : 16'bz;  // Controlled_Buffer controlled_buffer_2
  assign controlled_buffer_3_out = decoder_1_out2 ? multiplexer_2_out : 16'bz;  // Controlled_Buffer controlled_buffer_3
  assign controlled_buffer_4_out = decoder_1_out4 ? multiplexer_1_out : 16'bz;  // Controlled_Buffer controlled_buffer_4
  assign controlled_buffer_5_out = decoder_1_out4 ? multiplexer_2_out : 16'bz;  // Controlled_Buffer controlled_buffer_5
  Decoder #(.select(3)) decoder_1 (
    .out0(decoder_1_out0), .out1(decoder_1_out1), .out2(decoder_1_out2), .out3(decoder_1_out3),
    .out4(decoder_1_out4), .sel(out_8[2:0]));  // open: out5, out6, out7, en
  assign controlled_buffer_6_out = decoder_1_out0 ? multiplexer_1_out : 16'bz;  // Controlled_Buffer controlled_buffer_6
  assign controlled_buffer_7_out = decoder_1_out0 ? multiplexer_2_out : 16'bz;  // Controlled_Buffer controlled_buffer_7
  assign not_2_out = ~controlled_buffer_1_out;  // NOT_Gate not_2, 16 bits wide
  Decoder #(.select(3)) decoder_2 (
    .out0(decoder_2_out0), .out1(decoder_2_out1), .out2(decoder_2_out2), .out3(decoder_2_out3),
    .out4(decoder_2_out4), .out5(decoder_2_out5), .sel(out_8[11:9]));  // open: out6, out7, en
  assign nor_1_out = ~(controlled_buffer_6_out | controlled_buffer_7_out);  // NOR_Gate nor_1, 16 bits wide
  Multiplier #(.width(16)) multiplier_1 (
    .a(controlled_buffer_2_out), .b(controlled_buffer_3_out), .out(multiplier_1_out));  // open: cin, cout
  assign xor_1_out = controlled_buffer_4_out ^ controlled_buffer_5_out;  // XOR_Gate xor_1, 16 bits wide
  Multiplexer #(.select(3), .width(16)) multiplexer_3 (
    .in0(nor_1_out), .in1(not_2_out), .in2(multiplier_1_out), .in3(xor_1_out), .in4(multiplexer_1_out),
    .out(multiplexer_3_out), .sel(out_8[2:0]));  // open: in5, in6, in7, en
  Clock clock_1 (.out(clock_1_out));
  Multiplexer #(.width(12)) multiplexer_4 (
    .in0(register_1_q[11:0]), .in1(counter_1_q), .out(multiplexer_4_out), .sel(or_2_out));  // open: en
  or or_1 (or_1_out, decoder_2_out1, and_1_out);
  Register #(.width(16)) register_1 (
    .D(multiplexer_3_out), .en(or_1_out), .Q(register_1_q), .clk(not_3_out), .clr(decoder_1_out3));
  Register #(.width(16)) register_2 (
    .D(multiplexer_3_out), .en(decoder_2_out2), .Q(register_2_q), .clk(not_3_out), .clr(in_6));
  Register #(.width(16)) register_3 (
    .D(multiplexer_3_out), .en(decoder_2_out3), .Q(register_3_q), .clk(not_3_out), .clr(decoder_2_out4));
  not not_3 (not_3_out, clock_1_out);
  RAM #(.addrWidth(12), .dataWidth(16)) ram_1 (
    .addr(multiplexer_4_out), .data({ram_1_data[15], out_7[5:3], ram_1_data[11:0]}));  // open: sel, clk, ld, clr
  or or_2 (or_2_out, and_4_out, and_2_out);
  and and_2 (and_2_out, out_8[0], out_8[1], out_8[2]);
  Register #(.width(1), .trigger("falling")) register_4 (
    .D(ram_1_data[15]), .Q(register_4_q), .clk(clock_1_out));  // open: en, clr
  not not_4 (not_4_out, and_2_out);
  Counter #(.width(7), .max('h7f), .trigger("falling")) counter_2 (
    .load(and_2_out), .D({in_4, out_7[5:3], {3{in_4}}}), .count(not_4_out), .Q(counter_2_q),
    .clk(clock_1_out), .clr(in_5));  // open: carry
  ROM #(.addrWidth(7), .dataWidth(12)) rom_1 (.addr(counter_2_q), .data(out_8));  // open: sel
  and and_3 (and_3_out, out_8[2], out_8[5], out_8[8], out_8[9]);
  not not_5 (not_5_out, or_3_out);
  or or_3 (or_3_out, out_8[0], out_8[1], out_8[3], out_8[4], out_8[6], out_8[7], out_8[10], out_8[11]);
  and and_4 (and_4_out, and_3_out, not_5_out);

  assign {out_7[6], out_7[2:0]} = {4{in_4}};

  // Notes on the sheet:
  //   AR
  //   AC
  //   DR
  //   contents of rom_1 (hex, n*v repeats v):
  //   324 b24 604 4d0 fff 0 0 0 324 b24 604 6d9 fff 0 0 0 324 b24 604 49a fff 0 0 0 324 b24 604 694 fff 0
  //   0 0 324 b24 604 49b fff 0 0 0 800 fff
endmodule
